# Fritzing sketch Litterbox (saved by Fritzing 0.9.6b)
circuit board: 8.46667cm x 5.64444cm
breadboards: 1

parts:
  U1 = NodeMCU V1.0
  DHT11-1 = DHT11 Humitidy and Temperature Sensor
  PIR-1 = HC-SR501 Body Sensor Module
  R3 = Resistor [tolerance=±5% power=0.25 resistance=10k package=THT]
  S1 = Pushbutton [package="[THT]"]
  R2 = Resistor [tolerance=±5% power=0.25 resistance=10k package=THT]
  LCD-1 = LCD1602-I2C
  R1 = Resistor [tolerance=±5% power=0.25 resistance=220 package=THT]
  LED1 = LED - 5mm [color="Red (633nm)" current=0.030 package="5 mm [THT]"]
  5VDC = DC Power [voltage=5]

nets:
  N1: U1.D1, LCD-1.SCL
  N2: U1.D2, LCD-1.SDA
  N3: U1.D4, R1.Pin_1
  3V3: U1.3V3, DHT11-1.VDD, S1.Pin_1, S1.Pin_2, R2.Pin_0
  GND: U1.GND, DHT11-1.GND, PIR-1.GND, R3.Pin_0, LCD-1.GND, LED1.cathode, 5VDC.V-
  N4: U1.D5, DHT11-1.DATA
  N5: U1.D6, PIR-1.OUT, R2.Pin_1
  N6: U1.D7, R3.Pin_1, S1.Pin_3, S1.Pin_4
  VCC: U1.Vin, PIR-1.VCC, LCD-1.VCC, 5VDC.V+
  N7: R1.Pin_0, LED1.anode

custom parts:
  NodeMCU V1.0: ESP8266 based NodeMCU
  DHT11 Humitidy and Temperature Sensor: DHT11 Humidity and Temperature Sensor
  HC-SR501 Body Sensor Module: Pyroelectric Infrared PIR Motion Sensor Detector Module
  LCD1602-I2C: A standard character display, usually with 2x16 characters. Comes in many colors with LCM1602 IIC attached.
